// Logisim project CPU.circ as structural Verilog: 16 circuits, main circuit main
module main (
  input  in_1,
  input  [9:0] _0,
  input  [9:0] _1,
  input  [9:0] _2,
  input  [9:0] _3,
  input  [9:0] _4,
  input  RST,
  input  [9:0] _5,
  input  [9:0] _6,
  input  [9:0] _7,
  input  [9:0] _8,
  input  [9:0] _9,
  input  [9:0] _10,
  input  [9:0] _11,
  input  [9:0] _12,
  input  [9:0] _13,
  input  [9:0] _14,
  input  [9:0] _15,
  input  [9:0] _16,
  input  [9:0] _17,
  input  [9:0] _18,
  input  [9:0] _19,
  input  [9:0] _20,
  input  [9:0] _21,
  input  [9:0] _22,
  input  [9:0] _23,
  input  [9:0] _24,
  input  [9:0] _25,
  input  [9:0] _26,
  input  [9:0] _27,
  input  [9:0] _28,
  input  [9:0] _29,
  input  [9:0] _30,
  input  [9:0] _31,
  output [7:0] R_0,
  output [7:0] R_1,
  output [7:0] R_2,
  output [7:0] R_3,
  output [7:0] out_39,
  output [4:0] out_40
);

  wire and_1_out, CLK_out, decoder_1_goto_ctrl, decoder_1_mux_ctrl, decoder_1_reg_ctrl, decoder_1_var_ctrl,
       flags_1_goto;
  wire [1:0] decoder_1_out_7, decoder_1_ra, decoder_1_rb, decoder_1_rc, ir_1_instruction;
  wire [4:0] add_5_1_out_2, branch_1_out_3, multiplexer_2_out, n8_5_convert_1_out_2, pc_1_pc_2;
  wire [7:0] alu_1_f1, alu_1_f2, decoder_1_var, ir_1_data, multiplexer_1_out, registers_1_a, registers_1_b,
       var_1_var_2;

  REGISTERS registers_1 (
    .DATA_IN(alu_1_f1), .RC(decoder_1_rc), .B(registers_1_b), .A(registers_1_a), .CTRL(decoder_1_reg_ctrl),
    .RB(decoder_1_rb), .RA(decoder_1_ra), .CLK(CLK_out), .RST(in_1), .R_1(R_1), .R_2(R_2), .R_3(R_3),
    .R_0(R_0));
  Multiplexer #(.width(8)) multiplexer_1 (
    .in0(registers_1_b), .in1(var_1_var_2), .out(multiplexer_1_out), .sel(decoder_1_mux_ctrl));  // open: en
  ALU alu_1 (.in_3(decoder_1_out_7), .B(multiplexer_1_out), .A(registers_1_a), .F1(alu_1_f1), .F2(alu_1_f2));
  VAR var_1 (.CTRL(decoder_1_var_ctrl), .VAR_IN(decoder_1_var), .VAR_2(var_1_var_2), .CLK(CLK_out), .VAR(out_39));
  FLAGS flags_1 (.DATA(alu_1_f2), .GOTO(flags_1_goto), .in_1(decoder_1_out_7));
  DECODER decoder_1 (
    .RC(decoder_1_rc), .RB(decoder_1_rb), .RA(decoder_1_ra), .VAR(decoder_1_var), .out_7(decoder_1_out_7),
    .REG_CTRL(decoder_1_reg_ctrl), .VAR_CTRL(decoder_1_var_ctrl), .MUX_CTRL(decoder_1_mux_ctrl),
    .GOTO_CTRL(decoder_1_goto_ctrl), .INSTRUCTION(ir_1_data), .TYPE(ir_1_instruction));
  IR ir_1 (
    .DATA(ir_1_data), .INSTRUCTION(ir_1_instruction), .PC(pc_1_pc_2), .in_2(_0), .in_3(_1), .in_4(_2),
    .in_5(_3), .in_6(_4), .in_7(_5), .in_8(_6), .in_9(_7), .in_10(_8), .in_11(_9), .in_12(_10), .in_13(_11),
    .in_14(_12), .in_15(_13), .in_16(_14), .in_17(_15), .in_18(_16), .in_19(_17), .in_20(_18), .in_21(_19),
    .in_22(_20), .in_23(_21), .in_24(_22), .in_25(_23), .in_26(_24), .in_27(_25), .in_28(_26), .in_29(_27),
    .in_30(_28), .in_31(_29), .in_32(_30), .in_33(_31));
  PC pc_1 (.PC_2(pc_1_pc_2), .CLK(CLK_out), .NEW(multiplexer_2_out), .RST(RST), .PC(out_40));
  ADD_5 add_5_1 (.A(pc_1_pc_2), .out_2(add_5_1_out_2));
  Clock CLK (.out(CLK_out));
  Multiplexer #(.width(5)) multiplexer_2 (
    .in0(add_5_1_out_2), .in1(branch_1_out_3), .out(multiplexer_2_out), .sel(and_1_out));  // open: en
  and and_1 (and_1_out, decoder_1_goto_ctrl, flags_1_goto);
  BRANCH branch_1 (.A(pc_1_pc_2), .B(n8_5_convert_1_out_2), .out_3(branch_1_out_3));
  _8_5_CONVERT u_8_5_convert_1 (.in_1(var_1_var_2), .out_2(n8_5_convert_1_out_2));
endmodule

// ADD
module ADD_1 (
  input  A,
  input  B,
  input  Cin,
  output S,
  output Cout
);

  wire and_1_out, and_2_out, xor_1_out;

  xor xor_1 (xor_1_out, A, B);
  and and_1 (and_1_out, A, B);
  xor xor_2 (S, xor_1_out, Cin);
  and and_2 (and_2_out, xor_1_out, Cin);
  or or_1 (Cout, and_2_out, and_1_out);
endmodule

// ADD
module ADD_8 (
  input  [7:0] A,
  input  [7:0] B,
  output [7:0] out_3,
  output OVERFLOW
);

  wire add_1_1_cout, add_1_2_cout, add_1_3_cout, add_1_4_cout, add_1_5_cout, add_1_6_cout, add_1_7_cout;

  ADD_1 add_1_1 (.A(A[0]), .B(B[0]), .Cin(1'b0), .S(out_3[0]), .Cout(add_1_1_cout));
  ADD_1 add_1_2 (.A(A[1]), .B(B[1]), .Cin(add_1_1_cout), .S(out_3[1]), .Cout(add_1_2_cout));
  ADD_1 add_1_3 (.A(A[2]), .B(B[2]), .Cin(add_1_2_cout), .S(out_3[2]), .Cout(add_1_3_cout));
  ADD_1 add_1_4 (.A(A[4]), .B(B[4]), .Cin(add_1_5_cout), .S(out_3[4]), .Cout(add_1_4_cout));
  ADD_1 add_1_5 (.A(A[3]), .B(B[3]), .Cin(add_1_3_cout), .S(out_3[3]), .Cout(add_1_5_cout));
  ADD_1 add_1_6 (.A(A[5]), .B(B[5]), .Cin(add_1_4_cout), .S(out_3[5]), .Cout(add_1_6_cout));
  ADD_1 add_1_7 (.A(A[6]), .B(B[6]), .Cin(add_1_6_cout), .S(out_3[6]), .Cout(add_1_7_cout));
  ADD_1 add_1_8 (.A(A[7]), .B(B[7]), .Cin(add_1_7_cout), .S(out_3[7]), .Cout(OVERFLOW));
endmodule

// SUB
module SUB_8 (
  input  [7:0] A,
  input  [7:0] B,
  output [7:0] out_3,
  output OVERFLOW
);

  wire add_1_1_cout, add_1_2_cout, add_1_3_cout, add_1_4_cout, add_1_5_cout, add_1_6_cout, add_1_7_cout,
       xor_1_out, xor_2_out, xor_3_out, xor_4_out, xor_5_out, xor_6_out, xor_7_out, xor_8_out;

  xor xor_1 (xor_1_out, 1'b1, B[0]);
  ADD_1 add_1_1 (.A(A[0]), .B(xor_1_out), .Cin(1'b1), .S(out_3[0]), .Cout(add_1_1_cout));
  xor xor_2 (xor_2_out, 1'b1, B[1]);
  ADD_1 add_1_2 (.A(A[1]), .B(xor_2_out), .Cin(add_1_1_cout), .S(out_3[1]), .Cout(add_1_2_cout));
  xor xor_3 (xor_3_out, 1'b1, B[2]);
  ADD_1 add_1_3 (.A(A[2]), .B(xor_3_out), .Cin(add_1_2_cout), .S(out_3[2]), .Cout(add_1_3_cout));
  xor xor_4 (xor_4_out, 1'b1, B[3]);
  ADD_1 add_1_4 (.A(A[3]), .B(xor_4_out), .Cin(add_1_3_cout), .S(out_3[3]), .Cout(add_1_4_cout));
  ADD_1 add_1_5 (.A(A[4]), .B(xor_5_out), .Cin(add_1_4_cout), .S(out_3[4]), .Cout(add_1_5_cout));
  xor xor_5 (xor_5_out, 1'b1, B[4]);
  ADD_1 add_1_6 (.A(A[5]), .B(xor_6_out), .Cin(add_1_5_cout), .S(out_3[5]), .Cout(add_1_6_cout));
  xor xor_6 (xor_6_out, 1'b1, B[5]);
  ADD_1 add_1_7 (.A(A[6]), .B(xor_7_out), .Cin(add_1_6_cout), .S(out_3[6]), .Cout(add_1_7_cout));
  xor xor_7 (xor_7_out, 1'b1, B[6]);
  ADD_1 add_1_8 (.A(A[7]), .B(xor_8_out), .Cin(add_1_7_cout), .S(out_3[7]), .Cout(OVERFLOW));
  xor xor_8 (xor_8_out, 1'b1, B[7]);
endmodule

module ALU (
  input  [7:0] B,
  input  [7:0] A,
  input  [1:0] in_3,
  output [7:0] F1,
  output [7:0] F2
);

  wire [7:0] add_8_1_out_3;

  ADD_8 add_8_1 (.A(A), .B(B), .out_3(add_8_1_out_3));  // open: OVERFLOW
  Multiplexer #(.select(2), .width(8)) multiplexer_1 (
    .in0(add_8_1_out_3), .in1(F2), .in2(A), .in3(B), .out(F1), .sel(in_3));  // open: en
  SUB_8 sub_8_1 (.A(A), .B(B), .out_3(F2));  // open: OVERFLOW
endmodule

module FLAGS (
  input  [1:0] in_1,
  input  [7:0] DATA,
  output GOTO
);

  wire and_1_out, not_1_out, not_2_out, or_1_out, or_2_out;

  not not_1 (not_1_out, DATA[7]);
  or or_1 (or_1_out, DATA[7], DATA[6], DATA[5], DATA[4], DATA[3], DATA[2], DATA[1], DATA[0]);
  not not_2 (not_2_out, or_1_out);
  and and_1 (and_1_out, or_1_out, not_1_out);
  or or_2 (or_2_out, not_1_out, not_2_out);
  Multiplexer #(.select(2)) multiplexer_1 (
    .in0(and_1_out), .in1(DATA[7]), .in2(or_2_out), .in3(not_2_out), .out(GOTO), .sel(in_1));  // open: en

  // Notes on the sheet:
  //   A - B
endmodule

module VAR (
  input  [7:0] VAR_IN,
  input  CTRL,
  input  CLK,
  output [7:0] VAR,
  output [7:0] VAR_2
);

  Register register_1 (.D(VAR_IN), .en(CTRL), .Q(VAR), .clk(CLK));  // open: clr

  assign VAR_2 = VAR;
endmodule

module D_Latch (
  input  Q,
  input  D,
  output Q_prime
);

  wire and_1_out, and_2_out, nor_2_out, not_1_out;

  not not_1 (not_1_out, D);
  and and_1 (and_1_out, not_1_out, Q);
  and and_2 (and_2_out, Q, D);
  nor nor_1 (Q_prime, and_1_out, nor_2_out);
  nor nor_2 (nor_2_out, Q_prime, and_2_out);
endmodule

module REGISTERS (
  input  CTRL,
  input  [1:0] RC,
  input  [7:0] DATA_IN,
  input  [1:0] RB,
  input  [1:0] RA,
  input  CLK,
  input  RST,
  output [7:0] B,
  output [7:0] A,
  output [7:0] R_0,
  output [7:0] R_1,
  output [7:0] R_2,
  output [7:0] R_3
);

  wire and_1_out, and_2_out, and_3_out, and_4_out, decoder_1_out0, decoder_1_out1, decoder_1_out2,
       decoder_1_out3;

  Decoder #(.select(2)) decoder_1 (
    .out0(decoder_1_out0), .out1(decoder_1_out1), .out2(decoder_1_out2), .out3(decoder_1_out3), .sel(RC));  // open: en
  Register register_1 (.D(DATA_IN), .en(and_1_out), .Q(R_0), .clk(CLK), .clr(RST));
  and and_1 (and_1_out, CTRL, decoder_1_out0);
  Register register_2 (.D(DATA_IN), .en(and_2_out), .Q(R_1), .clk(CLK), .clr(RST));
  and and_2 (and_2_out, CTRL, decoder_1_out1);
  Register register_3 (.D(DATA_IN), .en(and_3_out), .Q(R_2), .clk(CLK), .clr(RST));
  and and_3 (and_3_out, CTRL, decoder_1_out2);
  Register register_4 (.D(DATA_IN), .en(and_4_out), .Q(R_3), .clk(CLK), .clr(RST));
  and and_4 (and_4_out, CTRL, decoder_1_out3);
  Multiplexer #(.select(2), .width(8)) multiplexer_1 (
    .in0(R_0), .in1(R_1), .in2(R_2), .in3(R_3), .out(B), .sel(RB));  // open: en
  Multiplexer #(.select(2), .width(8)) multiplexer_2 (
    .in0(R_0), .in1(R_1), .in2(R_2), .in3(R_3), .out(A), .sel(RA));  // open: en
endmodule

module DECODER (
  input  [7:0] INSTRUCTION,
  input  [1:0] TYPE,
  output [1:0] RC,
  output [1:0] RB,
  output [1:0] RA,
  output [7:0] VAR,
  output [1:0] out_7,
  output REG_CTRL,
  output VAR_CTRL,
  output MUX_CTRL,
  output GOTO_CTRL
);

  wire not_1_out;

  xor xor_1 (REG_CTRL, TYPE[0], TYPE[1]);
  nor nor_1 (VAR_CTRL, TYPE[0], TYPE[1]);
  not not_1 (not_1_out, TYPE[0]);
  and and_1 (MUX_CTRL, not_1_out, TYPE[1]);
  and and_2 (GOTO_CTRL, TYPE[0], TYPE[1]);

  assign out_7 = INSTRUCTION[7:6];
  assign RA = INSTRUCTION[5:4];
  assign RB = INSTRUCTION[3:2];
  assign RC = INSTRUCTION[1:0];
  assign VAR = INSTRUCTION;
endmodule

module IR (
  input  [4:0] PC,
  input  [9:0] in_2,
  input  [9:0] in_3,
  input  [9:0] in_4,
  input  [9:0] in_5,
  input  [9:0] in_6,
  input  [9:0] in_7,
  input  [9:0] in_8,
  input  [9:0] in_9,
  input  [9:0] in_10,
  input  [9:0] in_11,
  input  [9:0] in_12,
  input  [9:0] in_13,
  input  [9:0] in_14,
  input  [9:0] in_15,
  input  [9:0] in_16,
  input  [9:0] in_17,
  input  [9:0] in_18,
  input  [9:0] in_19,
  input  [9:0] in_20,
  input  [9:0] in_21,
  input  [9:0] in_22,
  input  [9:0] in_23,
  input  [9:0] in_24,
  input  [9:0] in_25,
  input  [9:0] in_26,
  input  [9:0] in_27,
  input  [9:0] in_28,
  input  [9:0] in_29,
  input  [9:0] in_30,
  input  [9:0] in_31,
  input  [9:0] in_32,
  input  [9:0] in_33,
  output [7:0] DATA,
  output [1:0] INSTRUCTION
);

  wire [9:0] register_1_var, register_2_var, register_3_var, register_4_var, register_5_var, register_6_var,
       register_7_var, register_8_var, register_9_var, register_10_var, register_11_var, register_12_var,
       register_13_var, register_14_var, register_15_var, register_16_var, register_17_var, register_18_var,
       register_19_var, register_20_var, register_21_var, register_22_var, register_23_var, register_24_var,
       register_25_var, register_26_var, register_27_var, register_28_var, register_29_var, register_30_var,
       register_31_var, register_32_var;

  Multiplexer #(.select(5), .width(10)) multiplexer_1 (
    .in0(register_1_var), .in1(register_2_var), .in2(register_3_var), .in3(register_4_var),
    .in4(register_5_var), .in5(register_6_var), .in6(register_7_var), .in7(register_8_var),
    .in8(register_9_var), .in9(register_10_var), .in10(register_11_var), .in11(register_12_var),
    .in12(register_13_var), .in13(register_14_var), .in14(register_15_var), .in15(register_16_var),
    .in16(register_17_var), .in17(register_18_var), .in18(register_19_var), .in19(register_20_var),
    .in20(register_21_var), .in21(register_22_var), .in22(register_23_var), .in23(register_24_var),
    .in24(register_25_var), .in25(register_26_var), .in26(register_27_var), .in27(register_28_var),
    .in28(register_29_var), .in29(register_30_var), .in30(register_31_var), .in31(register_32_var),
    .out({INSTRUCTION, DATA}), .sel(PC));  // open: en
  REGISTER register_1 (.VAR_IN(in_2), .CTRL(1'b1), .VAR(register_1_var));
  REGISTER register_2 (.VAR_IN(in_3), .CTRL(1'b1), .VAR(register_2_var));
  REGISTER register_3 (.VAR_IN(in_4), .CTRL(1'b1), .VAR(register_3_var));
  REGISTER register_4 (.VAR_IN(in_5), .CTRL(1'b1), .VAR(register_4_var));
  REGISTER register_5 (.VAR_IN(in_6), .CTRL(1'b1), .VAR(register_5_var));
  REGISTER register_6 (.VAR_IN(in_7), .CTRL(1'b1), .VAR(register_6_var));
  REGISTER register_7 (.VAR_IN(in_8), .CTRL(1'b1), .VAR(register_7_var));
  REGISTER register_8 (.VAR_IN(in_9), .CTRL(1'b1), .VAR(register_8_var));
  REGISTER register_9 (.VAR_IN(in_10), .CTRL(1'b1), .VAR(register_9_var));
  REGISTER register_10 (.VAR_IN(in_11), .CTRL(1'b1), .VAR(register_10_var));
  REGISTER register_11 (.VAR_IN(in_12), .CTRL(1'b1), .VAR(register_11_var));
  REGISTER register_12 (.VAR_IN(in_13), .CTRL(1'b1), .VAR(register_12_var));
  REGISTER register_13 (.VAR_IN(in_14), .CTRL(1'b1), .VAR(register_13_var));
  REGISTER register_14 (.VAR_IN(in_15), .CTRL(1'b1), .VAR(register_14_var));
  REGISTER register_15 (.VAR_IN(in_16), .CTRL(1'b1), .VAR(register_15_var));
  REGISTER register_16 (.VAR_IN(in_17), .CTRL(1'b1), .VAR(register_16_var));
  REGISTER register_17 (.VAR_IN(in_18), .CTRL(1'b1), .VAR(register_17_var));
  REGISTER register_18 (.VAR_IN(in_19), .CTRL(1'b1), .VAR(register_18_var));
  REGISTER register_19 (.VAR_IN(in_20), .CTRL(1'b1), .VAR(register_19_var));
  REGISTER register_20 (.VAR_IN(in_21), .CTRL(1'b1), .VAR(register_20_var));
  REGISTER register_21 (.VAR_IN(in_22), .CTRL(1'b1), .VAR(register_21_var));
  REGISTER register_22 (.VAR_IN(in_23), .CTRL(1'b1), .VAR(register_22_var));
  REGISTER register_23 (.VAR_IN(in_24), .CTRL(1'b1), .VAR(register_23_var));
  REGISTER register_24 (.VAR_IN(in_25), .CTRL(1'b1), .VAR(register_24_var));
  REGISTER register_25 (.VAR_IN(in_26), .CTRL(1'b1), .VAR(register_25_var));
  REGISTER register_26 (.VAR_IN(in_27), .CTRL(1'b1), .VAR(register_26_var));
  REGISTER register_27 (.VAR_IN(in_28), .CTRL(1'b1), .VAR(register_27_var));
  REGISTER register_28 (.VAR_IN(in_29), .CTRL(1'b1), .VAR(register_28_var));
  REGISTER register_29 (.VAR_IN(in_30), .CTRL(1'b1), .VAR(register_29_var));
  REGISTER register_30 (.VAR_IN(in_31), .CTRL(1'b1), .VAR(register_30_var));
  REGISTER register_31 (.VAR_IN(in_32), .CTRL(1'b1), .VAR(register_31_var));
  REGISTER register_32 (.VAR_IN(in_33), .CTRL(1'b1), .VAR(register_32_var));
endmodule

module REGISTER (
  input  [9:0] VAR_IN,
  input  CTRL,
  output [9:0] VAR
);

  D_Latch d_latch_1 (.Q(CTRL), .D(VAR_IN[0]), .Q_prime(VAR[0]));
  D_Latch d_latch_2 (.Q(CTRL), .D(VAR_IN[1]), .Q_prime(VAR[1]));
  D_Latch d_latch_3 (.Q(CTRL), .D(VAR_IN[2]), .Q_prime(VAR[2]));
  D_Latch d_latch_4 (.Q(CTRL), .D(VAR_IN[3]), .Q_prime(VAR[3]));
  D_Latch d_latch_5 (.Q(CTRL), .D(VAR_IN[4]), .Q_prime(VAR[4]));
  D_Latch d_latch_6 (.Q(CTRL), .D(VAR_IN[5]), .Q_prime(VAR[5]));
  D_Latch d_latch_7 (.Q(CTRL), .D(VAR_IN[6]), .Q_prime(VAR[6]));
  D_Latch d_latch_8 (.Q(CTRL), .D(VAR_IN[7]), .Q_prime(VAR[7]));
  D_Latch d_latch_9 (.Q(CTRL), .D(VAR_IN[8]), .Q_prime(VAR[8]));
  D_Latch d_latch_10 (.Q(CTRL), .D(VAR_IN[9]), .Q_prime(VAR[9]));
endmodule

module PC (
  input  [4:0] NEW,
  input  CLK,
  input  RST,
  output [4:0] PC,
  output [4:0] PC_2
);

  D_Flip_Flop d_ff_1 (.clk(CLK), .D(NEW[0]), .Q(PC[0]), .reset(RST));  // open: Qn, preset, en
  D_Flip_Flop d_ff_2 (.clk(CLK), .D(NEW[1]), .Q(PC[1]), .reset(RST));  // open: Qn, preset, en
  D_Flip_Flop d_ff_3 (.clk(CLK), .D(NEW[2]), .Q(PC[2]), .reset(RST));  // open: Qn, preset, en
  D_Flip_Flop d_ff_4 (.clk(CLK), .D(NEW[3]), .Q(PC[3]), .reset(RST));  // open: Qn, preset, en
  D_Flip_Flop d_ff_5 (.clk(CLK), .D(NEW[4]), .Q(PC[4]), .reset(RST));  // open: Qn, preset, en

  assign PC_2 = PC;
endmodule

// +1
module ADD_5 (
  input  [4:0] A,
  output [4:0] out_2
);

  wire add_1_1_cout, add_1_2_cout, add_1_3_cout, add_1_4_cout, add_1_5_cout;
  wire [4:0] add_1_1_s;

  ADD_1 add_1_1 (.A(A[0]), .B(1'b1), .Cin(1'b0), .S(add_1_1_s[0]), .Cout(add_1_1_cout));
  ADD_1 add_1_2 (.A(A[1]), .B(1'b0), .Cin(add_1_1_cout), .S(add_1_1_s[1]), .Cout(add_1_2_cout));
  ADD_1 add_1_3 (.A(A[2]), .B(1'b0), .Cin(add_1_2_cout), .S(add_1_1_s[2]), .Cout(add_1_3_cout));
  ADD_1 add_1_4 (.A(A[3]), .B(1'b0), .Cin(add_1_3_cout), .S(add_1_1_s[3]), .Cout(add_1_4_cout));
  ADD_1 add_1_5 (.A(A[4]), .B(1'b0), .Cin(add_1_4_cout), .S(add_1_1_s[4]), .Cout(add_1_5_cout));
  Multiplexer #(.width(5)) multiplexer_1 (
    .in0(add_1_1_s), .in1({5{1'b1}}), .out(out_2), .sel(add_1_5_cout));  // open: en
endmodule

module BRANCH (
  input  [4:0] A,
  input  [4:0] B,
  output [4:0] out_3
);

  wire add_1_1_cout, add_1_2_cout, add_1_3_cout, add_1_4_cout, and_1_out, or_1_out;
  wire [4:0] add_1_1_s;

  ADD_1 add_1_1 (.A(A[0]), .B(B[0]), .Cin(1'b0), .S(add_1_1_s[0]), .Cout(add_1_1_cout));
  ADD_1 add_1_2 (.A(A[1]), .B(B[1]), .Cin(add_1_1_cout), .S(add_1_1_s[1]), .Cout(add_1_2_cout));
  ADD_1 add_1_3 (.A(A[2]), .B(B[2]), .Cin(add_1_2_cout), .S(add_1_1_s[2]), .Cout(add_1_3_cout));
  ADD_1 add_1_4 (.A(A[3]), .B(B[3]), .Cin(add_1_3_cout), .S(add_1_1_s[3]), .Cout(add_1_4_cout));
  ADD_1 add_1_5 (.A(A[4]), .B(B[4]), .Cin(add_1_4_cout), .S(add_1_1_s[4]));  // open: Cout
  and and_1 (and_1_out, A[0], A[1], A[2], A[3], A[4]);
  // NOT_Gate not_1 has open pins: in=or_1_out, out=open
  or or_1 (or_1_out, add_1_1_s[0], add_1_1_s[1], add_1_1_s[2], add_1_1_s[3], add_1_1_s[4]);
  Multiplexer #(.width(5)) multiplexer_1 (.in0(add_1_1_s), .in1({5{1'b1}}), .out(out_3), .sel(and_1_out));  // open: en
endmodule

module _8_5_CONVERT (
  input  [7:0] in_1,
  output [4:0] out_2
);


  assign out_2 = in_1[4:0];
endmodule
